# Fritzing sketch file21,22 (saved by Fritzing 0.9.4)
breadboards: 1

parts:
  Part1 = Arduino Uno (Rev3)
  R1 = Resistor [tolerance=±5% resistance=220 package=THT]
  R2 = Resistor [tolerance=±5% resistance=220 package=THT]
  R3 = Resistor [tolerance=±5% resistance=220 package=THT]
  7_Segment1 = 7 Segment Display
  R4 = Resistor [tolerance=±5% resistance=220 package=THT]
  R5 = Resistor [tolerance=±5% resistance=220 package=THT]
  R6 = Resistor [tolerance=±5% resistance=220 package=THT]
  R7 = Resistor [tolerance=±5% resistance=220 package=THT]

nets:
  N1: Part1.D1/TX, R3.Pin_1
  N2: Part1.D2, R4.Pin_1
  N3: Part1.D3_PWM, R5.Pin_1
  N4: Part1.D4, R6.Pin_0
  N5: Part1.D5_PWM, R7.Pin_0
  N6: Part1.D6_PWM, R1.Pin_0
  N7: Part1.D7, R2.Pin_0
  N8: Part1.GND, 7_Segment1.common_anode
  N9: R1.Pin_1, 7_Segment1.Segment_F
  N10: R2.Pin_1, 7_Segment1.Segment_G
  N11: R3.Pin_0, 7_Segment1.Segment_A
  N12: 7_Segment1.Segment_E, R7.Pin_1
  N13: 7_Segment1.Segment_D, R6.Pin_1
  N14: 7_Segment1.Segment_C, R5.Pin_0
  N15: 7_Segment1.Segment_B, R4.Pin_0
