# Fritzing sketch file23,24 (saved by Fritzing 0.9.4)
breadboards: 1

parts:
  R1 = Photocell (LDR) [package=THT]
  R2 = Resistor [tolerance=±5% resistance=220 package=THT]
  LED1 = LED - 5mm [color="Red (633nm)" package="5 mm [THT]"]
  Part1 = Arduino Uno (Rev3)

nets:
  N1: R1.pin_0, R2.Pin_0, Part1.A0
  N2: R1.pin_1, Part1.5V
  N3: R2.Pin_1, LED1.cathode, Part1.GND
  N4: LED1.anode, Part1.D13/SCK
