# Fritzing sketch file25 (saved by Fritzing 0.9.4)
breadboards: 1

parts:
  S1 = Pushbutton [package="[THT]"]
  Part1 = Arduino Uno (Rev3)
  SP1 = SPEAKER [package=pcb_mount_speaker]

nets:
  N1: S1.Pin_1, S1.Pin_2, Part1.RESET
  N2: S1.Pin_3, S1.Pin_4, Part1.GND, SP1.+
  N3: Part1.D9_PWM, SP1.-
